// Logisim project circuit_F.3.circ as structural Verilog
module main (
  input  in_1,
  input  in_2,
  output out_3,
  output out_4,
  output out_5,
  output out_6
);

  wire not_1_out, not_2_out;

  not not_1 (not_1_out, in_1);
  not not_2 (not_2_out, in_2);
  and and_1 (out_3, not_1_out, not_2_out);
  and and_2 (out_4, in_1, not_2_out);
  and and_3 (out_5, not_1_out, in_2);
  and and_4 (out_6, in_1, in_2);
endmodule

module decoder_1_2 (
  input  in_1,
  output out_2,
  output out_3
);

  not not_1 (out_2, in_1);

  assign out_3 = in_1;
endmodule

module decoder_2_4 (
  input  in_1,
  input  in_2,
  output out_3,
  output out_4,
  output out_5,
  output out_6
);

  wire not_1_out, not_2_out;

  not not_1 (not_1_out, in_1);
  not not_2 (not_2_out, in_2);
  and and_1 (out_3, not_1_out, not_2_out);
  and and_2 (out_4, in_1, not_2_out);
  and and_3 (out_5, not_1_out, in_2);
  and and_4 (out_6, in_1, in_2);
endmodule

module decoder_3_8 (
  input  in_1,
  input  in_2,
  input  in_3,
  output out_4,
  output out_5,
  output out_6,
  output out_7,
  output out_8,
  output out_9,
  output out_10,
  output out_11
);

  wire decoder_2_4_1_out_3, decoder_2_4_1_out_4, decoder_2_4_1_out_5, decoder_2_4_1_out_6,
       decoder_2_4_2_out_3, decoder_2_4_2_out_4, decoder_2_4_2_out_5, decoder_2_4_2_out_6;

  decoder_2_4 decoder_2_4_1 (
    .in_1(in_1), .in_2(in_2), .out_3(decoder_2_4_1_out_3), .out_4(decoder_2_4_1_out_4),
    .out_5(decoder_2_4_1_out_5), .out_6(decoder_2_4_1_out_6));
  decoder_2_4 decoder_2_4_2 (
    .in_1(in_2), .in_2(in_3), .out_3(decoder_2_4_2_out_3), .out_4(decoder_2_4_2_out_4),
    .out_5(decoder_2_4_2_out_5), .out_6(decoder_2_4_2_out_6));
  and and_1 (out_4, decoder_2_4_1_out_3, decoder_2_4_2_out_3);
  and and_2 (out_5, decoder_2_4_1_out_4, decoder_2_4_2_out_3);
  and and_3 (out_6, decoder_2_4_1_out_5, decoder_2_4_2_out_4);
  and and_4 (out_7, decoder_2_4_1_out_6, decoder_2_4_2_out_4);
  and and_5 (out_8, decoder_2_4_1_out_3, decoder_2_4_2_out_5);
  and and_6 (out_9, decoder_2_4_1_out_4, decoder_2_4_2_out_5);
  and and_7 (out_10, decoder_2_4_1_out_5, decoder_2_4_2_out_6);
  and and_8 (out_11, decoder_2_4_1_out_6, decoder_2_4_2_out_6);
endmodule

module xor_fully_customized (
  input  in_1,
  input  in_2,
  input  in_3,
  output out_4
);

  wire transistor_1_out;

  Transistor transistor_1 (.in(in_1), .out(transistor_1_out), .gate(in_2));
  Transistor #(.\type ("n")) transistor_2 (.in(1'b0), .out(transistor_1_out), .gate(in_2));
  Transistor transistor_3 (.in(in_2), .out(out_4), .gate(in_3));
  Transistor #(.\type ("n")) transistor_4 (.in(transistor_1_out), .out(out_4), .gate(in_3));
  Transistor transistor_5 (.in(in_3), .out(out_4), .gate(in_2));
  Transistor #(.\type ("n")) transistor_6 (.in(in_3), .out(out_4), .gate(transistor_1_out));
endmodule

module xnor_fully_customized (
  input  in_1,
  input  in_2,
  input  in_3,
  output out_4
);

  wire transistor_1_out;

  Transistor #(.\type ("n")) transistor_1 (.in(1'b0), .out(transistor_1_out), .gate(in_1));
  Transistor transistor_2 (.in(in_2), .out(transistor_1_out), .gate(in_1));
  Transistor #(.\type ("n")) transistor_3 (.in(in_1), .out(out_4), .gate(in_3));
  Transistor transistor_4 (.in(transistor_1_out), .out(out_4), .gate(in_3));
  Transistor #(.\type ("n")) transistor_5 (.in(in_3), .out(out_4), .gate(in_1));
  Transistor transistor_6 (.in(in_3), .out(out_4), .gate(transistor_1_out));
endmodule

module decoder_7segment (
  input  A0,
  input  A1,
  input  A2,
  input  A3,
  output out_5,
  output out_6,
  output out_7,
  output out_8,
  output out_9,
  output out_10,
  output out_11,
  output out_12,
  output out_13,
  output out_14,
  output out_15,
  output out_16,
  output out_17,
  output out_18,
  output out_19,
  output out_20
);

  wire a_out, b_out, c_out, d_out, decoder_1_2_1_out_2, decoder_1_2_1_out_3, decoder_3_8_1_out_4,
       decoder_3_8_1_out_5, decoder_3_8_1_out_6, decoder_3_8_1_out_7, decoder_3_8_1_out_8,
       decoder_3_8_1_out_9, decoder_3_8_1_out_10, decoder_3_8_1_out_11, e_out, f_out, g_out, h_out;

  decoder_3_8 decoder_3_8_1 (
    .in_1(A0), .in_2(A1), .in_3(A2), .out_4(decoder_3_8_1_out_4), .out_5(decoder_3_8_1_out_5),
    .out_6(decoder_3_8_1_out_6), .out_7(decoder_3_8_1_out_7), .out_8(decoder_3_8_1_out_8),
    .out_9(decoder_3_8_1_out_9), .out_10(decoder_3_8_1_out_10), .out_11(decoder_3_8_1_out_11));
  decoder_1_2 decoder_1_2_1 (.in_1(A3), .out_2(decoder_1_2_1_out_2), .out_3(decoder_1_2_1_out_3));
  and C0 (out_5, decoder_3_8_1_out_4, decoder_1_2_1_out_2);
  and C1 (out_6, decoder_3_8_1_out_5, decoder_1_2_1_out_2);
  and C2 (out_7, decoder_3_8_1_out_6, decoder_1_2_1_out_2);
  and C3 (out_8, decoder_3_8_1_out_7, decoder_1_2_1_out_2);
  and C4 (out_9, decoder_3_8_1_out_8, decoder_1_2_1_out_2);
  and C5 (out_10, decoder_3_8_1_out_9, decoder_1_2_1_out_2);
  and C6 (out_11, decoder_3_8_1_out_10, decoder_1_2_1_out_2);
  and C7 (out_12, decoder_3_8_1_out_11, decoder_1_2_1_out_2);
  and C8 (out_13, decoder_3_8_1_out_4, decoder_1_2_1_out_3);
  and C9 (out_14, decoder_3_8_1_out_5, decoder_1_2_1_out_3);
  and C10 (out_15, decoder_3_8_1_out_6, decoder_1_2_1_out_3);
  and C11 (out_16, decoder_3_8_1_out_7, decoder_1_2_1_out_3);
  and C12 (out_17, decoder_3_8_1_out_8, decoder_1_2_1_out_3);
  and C13 (out_18, decoder_3_8_1_out_9, decoder_1_2_1_out_3);
  and C14 (out_19, decoder_3_8_1_out_10, decoder_1_2_1_out_3);
  and C16 (out_20, decoder_3_8_1_out_11, decoder_1_2_1_out_3);
  or h (h_out, out_15, out_16, out_17, out_18, out_19, out_20);
  or g (g_out, out_7, out_8, out_9, out_10, out_11, out_13, out_14);
  or f (f_out, out_5, out_9, out_10, out_11, out_13, out_14);
  or e (e_out, out_5, out_7, out_11, out_13);
  or d (d_out, out_5, out_7, out_8, out_10, out_11, out_13, out_14);
  or c (c_out, out_5, out_6, out_8, out_9, out_10, out_11, out_12, out_13, out_14);
  or b (b_out, out_5, out_6, out_7, out_8, out_9, out_12, out_13, out_14);
  or a (a_out, out_5, out_7, out_8, out_10, out_11, out_12, out_13, out_14);
  _7_Segment_Display u_7_segment_display_1 (
    .g(g_out), .f(f_out), .a(a_out), .b(b_out), .e(e_out), .d(d_out), .c(c_out), .dp(h_out));
endmodule

module decoder_hex_digit (
  input  A0,
  input  A1,
  input  A2,
  input  A3,
  output out_5,
  output out_6,
  output out_7,
  output out_8,
  output out_9,
  output out_10,
  output out_11,
  output out_12,
  output out_13,
  output out_14,
  output out_15,
  output out_16,
  output out_17,
  output out_18,
  output out_19,
  output out_20
);

  wire a_out, b_out, c_out, d_out, decoder_1_2_1_out_2, decoder_1_2_1_out_3, decoder_3_8_1_out_4,
       decoder_3_8_1_out_5, decoder_3_8_1_out_6, decoder_3_8_1_out_7, decoder_3_8_1_out_8,
       decoder_3_8_1_out_9, decoder_3_8_1_out_10, decoder_3_8_1_out_11, e_out, f_out, g_out;

  decoder_3_8 decoder_3_8_1 (
    .in_1(A0), .in_2(A1), .in_3(A2), .out_4(decoder_3_8_1_out_4), .out_5(decoder_3_8_1_out_5),
    .out_6(decoder_3_8_1_out_6), .out_7(decoder_3_8_1_out_7), .out_8(decoder_3_8_1_out_8),
    .out_9(decoder_3_8_1_out_9), .out_10(decoder_3_8_1_out_10), .out_11(decoder_3_8_1_out_11));
  decoder_1_2 decoder_1_2_1 (.in_1(A3), .out_2(decoder_1_2_1_out_2), .out_3(decoder_1_2_1_out_3));
  and C0 (out_5, decoder_3_8_1_out_4, decoder_1_2_1_out_2);
  and C1 (out_6, decoder_3_8_1_out_5, decoder_1_2_1_out_2);
  and C2 (out_7, decoder_3_8_1_out_6, decoder_1_2_1_out_2);
  and C3 (out_8, decoder_3_8_1_out_7, decoder_1_2_1_out_2);
  and C4 (out_9, decoder_3_8_1_out_8, decoder_1_2_1_out_2);
  and C5 (out_10, decoder_3_8_1_out_9, decoder_1_2_1_out_2);
  and C6 (out_11, decoder_3_8_1_out_10, decoder_1_2_1_out_2);
  and C7 (out_12, decoder_3_8_1_out_11, decoder_1_2_1_out_2);
  and C8 (out_13, decoder_3_8_1_out_4, decoder_1_2_1_out_3);
  and C9 (out_14, decoder_3_8_1_out_5, decoder_1_2_1_out_3);
  and C10 (out_15, decoder_3_8_1_out_6, decoder_1_2_1_out_3);
  and C11 (out_16, decoder_3_8_1_out_7, decoder_1_2_1_out_3);
  and C12 (out_17, decoder_3_8_1_out_8, decoder_1_2_1_out_3);
  and C13 (out_18, decoder_3_8_1_out_9, decoder_1_2_1_out_3);
  and C14 (out_19, decoder_3_8_1_out_10, decoder_1_2_1_out_3);
  and C15 (out_20, decoder_3_8_1_out_11, decoder_1_2_1_out_3);
  or g (g_out, out_7, out_8, out_9, out_10, out_11, out_13, out_14, out_15, out_16, out_18, out_19, out_20);
  or f (f_out, out_5, out_9, out_10, out_11, out_13, out_14, out_15, out_16, out_17, out_19, out_20);
  or e (e_out, out_5, out_7, out_11, out_13, out_15, out_16, out_17, out_18, out_19, out_20);
  or d (d_out, out_5, out_7, out_8, out_10, out_11, out_13, out_14, out_16, out_17, out_18, out_19);
  or c (c_out, out_5, out_6, out_8, out_9, out_10, out_11, out_12, out_13, out_14, out_15, out_16, out_18);
  or b (b_out, out_5, out_6, out_7, out_8, out_9, out_12, out_13, out_14, out_15, out_18);
  or a (a_out, out_5, out_7, out_8, out_10, out_11, out_12, out_13, out_14, out_15, out_17, out_19, out_20);
  _7_Segment_Display u_7_segment_display_1 (
    .g(g_out), .f(f_out), .a(a_out), .b(b_out), .e(e_out), .d(d_out), .c(c_out));  // open: dp
  Hex_Digit_Display hex_digit_display_1 ();  // open: value, dp
endmodule

module encoder_16to4 (
  input  A0,
  input  in_2,
  input  in_3,
  input  in_4,
  input  A4,
  input  in_6,
  input  in_7,
  input  in_8,
  input  A8,
  input  in_10,
  input  in_11,
  input  in_12,
  input  A12,
  input  in_14,
  input  in_15,
  input  in_16,
  output out_17,
  output out_18,
  output out_19,
  output out_20
);

  or B0 (out_17, in_2, in_4, in_6, in_8, in_10, in_12, in_14, in_16);
  or B1 (out_18, in_3, in_4, in_7, in_8, in_11, in_12, in_15, in_16);
  or B2 (out_19, A4, in_6, in_7, in_8, A12, in_14, in_15, in_16);
  or B3 (out_20, A8, in_10, in_11, in_12, A12, in_14, in_15, in_16);
endmodule

module encoder_4to2 (
  input  A0,
  input  A1,
  input  A2,
  input  A3,
  output Y0,
  output Y1
);

  or or_1 (Y0, A1, A3);
  or or_2 (Y1, A2, A3);
endmodule

module prior_encoder_4to2 (
  input  A0,
  input  A1,
  input  A2,
  input  A3,
  output Y0,
  output Y1
);

  wire and_1_out, and_2_out;

  and and_1 (and_1_out, A1, ~A2, ~A3);  // AND_Gate
  and and_2 (and_2_out, A2, ~A3);  // AND_Gate
  or or_1 (Y0, and_1_out, A3);
  or or_2 (Y1, and_2_out, A3);
endmodule

module prior_encoder_16to4 (
);

  wire prior_encoder_4to2_1_y0, prior_encoder_4to2_1_y1, prior_encoder_4to2_2_y0, prior_encoder_4to2_2_y1,
       prior_encoder_4to2_3_y0, prior_encoder_4to2_3_y1, prior_encoder_4to2_4_y0, prior_encoder_4to2_4_y1;

  prior_encoder_4to2 prior_encoder_4to2_1 (
    .Y0(prior_encoder_4to2_1_y0), .Y1(prior_encoder_4to2_1_y1));  // open: A0, A1, A2, A3
  prior_encoder_4to2 prior_encoder_4to2_2 (
    .Y0(prior_encoder_4to2_2_y0), .Y1(prior_encoder_4to2_2_y1));  // open: A0, A1, A2, A3
  prior_encoder_4to2 prior_encoder_4to2_3 (
    .Y0(prior_encoder_4to2_3_y0), .Y1(prior_encoder_4to2_3_y1));  // open: A0, A1, A2, A3
  prior_encoder_4to2 prior_encoder_4to2_4 (
    .Y0(prior_encoder_4to2_4_y0), .Y1(prior_encoder_4to2_4_y1));  // open: A0, A1, A2, A3
  // OR_Gate or_1 has open pins: in0=prior_encoder_4to2_1_y0, in1=prior_encoder_4to2_1_y1, out=open
  // OR_Gate or_2 has open pins: in0=prior_encoder_4to2_2_y0, in1=prior_encoder_4to2_2_y1, out=open
  // OR_Gate or_3 has open pins: in0=prior_encoder_4to2_3_y0, in1=prior_encoder_4to2_3_y1, out=open
  // OR_Gate or_4 has open pins: in0=prior_encoder_4to2_4_y0, in1=prior_encoder_4to2_4_y1, out=open
endmodule

module mux_2to1 (
  input  D0,
  input  S,
  input  D1,
  output out_4
);

  wire and_1_out, and_2_out, decoder_1_2_1_out_2, decoder_1_2_1_out_3;

  decoder_1_2 decoder_1_2_1 (.in_1(S), .out_2(decoder_1_2_1_out_2), .out_3(decoder_1_2_1_out_3));
  and and_1 (and_1_out, D0, decoder_1_2_1_out_2);
  and and_2 (and_2_out, decoder_1_2_1_out_3, D1);
  or or_1 (out_4, and_1_out, and_2_out);
endmodule

module mux_4to1 (
  input  in_1,
  input  in_2,
  input  in_3,
  input  in_4,
  input  in_5,
  input  in_6,
  input  in_7,
  output out_8
);

  wire and_1_out, and_2_out, and_3_out, and_4_out, decoder_3_8_1_out_4, decoder_3_8_1_out_5,
       decoder_3_8_1_out_6, decoder_3_8_1_out_7;

  decoder_3_8 decoder_3_8_1 (
    .in_1(in_3), .in_2(in_4), .in_3(in_5), .out_4(decoder_3_8_1_out_4), .out_5(decoder_3_8_1_out_5),
    .out_6(decoder_3_8_1_out_6), .out_7(decoder_3_8_1_out_7));  // open: out_8, out_9, out_10, out_11
  and and_1 (and_1_out, in_1, decoder_3_8_1_out_4);
  and and_2 (and_2_out, in_2, decoder_3_8_1_out_5);
  and and_3 (and_3_out, decoder_3_8_1_out_6, in_6);
  and and_4 (and_4_out, decoder_3_8_1_out_7, in_7);
  or or_1 (out_8, and_1_out, and_2_out, and_3_out, and_4_out);
endmodule

module comparator_4bit (
  input  in_1,
  input  in_2,
  input  in_3,
  input  in_4,
  input  in_5,
  input  in_6,
  input  in_7,
  input  in_8
);

  wire and_1_out, xnor_1_out, xnor_2_out, xnor_3_out, xnor_4_out;

  xnor xnor_1 (xnor_1_out, in_1, in_2);
  xnor xnor_2 (xnor_2_out, in_3, in_4);
  xnor xnor_3 (xnor_3_out, in_5, in_6);
  xnor xnor_4 (xnor_4_out, in_7, in_8);
  and and_1 (and_1_out, xnor_1_out, xnor_2_out, xnor_3_out, xnor_4_out);
  LED led_1 (.in(and_1_out));
endmodule

module adder_1_bit_full (
  input  Cin,
  input  A,
  input  B,
  output S,
  output Cout
);

  wire and_1_out, and_2_out, or_1_out, xor_1_out;

  and and_1 (and_1_out, ~Cin, A, B);  // AND_Gate
  or or_1 (or_1_out, A, B);
  xor xor_1 (xor_1_out, A, B);
  xor xor_2 (S, Cin, xor_1_out);
  or or_2 (Cout, and_1_out, and_2_out);
  and and_2 (and_2_out, Cin, or_1_out);
endmodule

module adder_1bit_half (
  input  A,
  input  B,
  output S,
  output C
);

  xor xor_1 (S, A, B);
  and and_1 (C, A, B);
endmodule

module adder_1bit_full_2 (
  input  Cin,
  input  A,
  input  B,
  output S,
  output Cout
);

  wire adder_1bit_half_1_c, adder_1bit_half_1_s, adder_1bit_half_2_c;

  adder_1bit_half adder_1bit_half_1 (.A(A), .B(B), .S(adder_1bit_half_1_s), .C(adder_1bit_half_1_c));
  adder_1bit_half adder_1bit_half_2 (.A(Cin), .B(adder_1bit_half_1_s), .S(S), .C(adder_1bit_half_2_c));
  xor xor_1 (Cout, adder_1bit_half_2_c, adder_1bit_half_1_c);
endmodule
